// Logisim project 1.1.3.circ as structural Verilog: 1 circuit, main circuit main
module main (
  input  A,
  input  B,
  input  C,
  input  D,
  output Y
);

  wire not_1_out, not_2_out, or_1_out, or_2_out, or_3_out;

  not not_1 (not_1_out, A);
  not not_2 (not_2_out, B);
  or or_1 (or_1_out, not_1_out, C);
  or or_2 (or_2_out, not_1_out, not_2_out, D);
  or or_3 (or_3_out, not_2_out, C, D);
  and and_1 (Y, or_1_out, or_2_out, or_3_out);
endmodule
