// Logisim project 1.3.3.1.circ as structural Verilog
module full_adder (
  input  in_1,
  input  in_2,
  input  in_3,
  output out_4,
  output out_5
);

  wire half_adder_1_out_3, half_adder_1_out_4, half_adder_2_out_4;

  half_adder half_adder_1 (.in_1(in_2), .in_2(in_3), .out_4(half_adder_1_out_4), .out_3(half_adder_1_out_3));
  or or_1 (out_5, half_adder_1_out_4, half_adder_2_out_4);
  half_adder half_adder_2 (.in_1(half_adder_1_out_3), .in_2(in_1), .out_4(half_adder_2_out_4), .out_3(out_4));
endmodule
