// Logisim project 1.1.2.circ as structural Verilog: 1 circuit, main circuit main
module main (
  input  A,
  input  B,
  input  C,
  output Y1,
  output Y2,
  output Y3
);

  wire and_1_out, and_2_out, and_3_out, and_4_out, and_5_out, not_1_out, not_2_out, not_3_out, not_4_out,
       not_5_out, not_6_out, xor_1_out;

  not not_1 (not_1_out, B);
  not not_2 (not_2_out, C);
  not not_3 (not_3_out, A);
  not not_4 (not_4_out, C);
  not not_5 (not_5_out, A);
  not not_6 (not_6_out, B);
  and and_1 (and_1_out, A, not_1_out, not_2_out);
  and and_2 (and_2_out, not_3_out, B, not_4_out);
  and and_3 (and_3_out, not_5_out, not_6_out, C);
  and and_4 (and_4_out, A, B, C);
  ExactlyOne xor_1 (.out(xor_1_out), .in0(A), .in1(B), .in2(C));
  and and_5 (and_5_out, A, B, C);
  ExactlyOne xor_2 (.out(Y3), .in0(A), .in1(B), .in2(C));
  or or_1 (Y1, and_1_out, and_2_out, and_3_out, and_4_out);
  or or_2 (Y2, xor_1_out, and_5_out);
endmodule
