// Logisim project 1.2.3.2.circ as structural Verilog: 3 circuits, main circuit main
module main (
  input  in_1,
  input  in_2,
  input  in_3,
  input  in_4,
  input  in_5,
  input  in_6,
  output out_7
);

  mux1 mux1_1 (.in_1(in_1), .in_2(in_2), .in_3(in_3), .in_4(in_4), .in_5(in_5), .in_6(in_6), .out_7(out_7));
endmodule

module mux0 (
  input  in_1,
  input  in_2,
  input  in_3,
  output out_4
);

  wire and_1_out, and_2_out;

  and and_1 (and_1_out, in_1, ~in_3);  // AND_Gate
  and and_2 (and_2_out, in_3, in_2);
  or or_1 (out_4, and_1_out, and_2_out);
endmodule

module mux1 (
  input  in_1,
  input  in_2,
  input  in_3,
  input  in_4,
  input  in_5,
  input  in_6,
  output out_7
);

  wire mux0_1_out_4, mux0_2_out_4;

  mux0 mux0_1 (.in_1(in_1), .in_2(in_2), .out_4(mux0_1_out_4), .in_3(in_6));
  mux0 mux0_2 (.in_1(in_3), .in_2(in_4), .out_4(mux0_2_out_4), .in_3(in_6));
  mux0 mux0_3 (.in_1(mux0_1_out_4), .in_2(mux0_2_out_4), .out_4(out_7), .in_3(in_5));
endmodule
