// Logisim project 1.3.1.2.circ as structural Verilog: 2 circuits, main circuit main
module main (
  input  in_1,
  input  in_2,
  input  in_3,
  output out_4,
  output out_5,
  output out_6,
  output out_7,
  output out_8,
  output out_9,
  output out_10,
  output out_11
);

  decoder_3 decoder_3_1 (
    .in_1(in_1), .in_2(in_2), .in_3(in_3), .out_4(out_4), .out_5(out_5), .out_6(out_6), .out_7(out_7),
    .out_8(out_8), .out_9(out_9), .out_10(out_10), .out_11(out_11));
endmodule

module decoder_3 (
  input  in_1,
  input  in_2,
  input  in_3,
  output out_4,
  output out_5,
  output out_6,
  output out_7,
  output out_8,
  output out_9,
  output out_10,
  output out_11
);

  wire not_1_out;

  decoder_2e decoder_2e_1 (
    .in_1(in_2), .in_2(in_3), .in_3(not_1_out), .out_4(out_4), .out_5(out_5), .out_6(out_6), .out_7(out_7));
  not not_1 (not_1_out, in_1);
  decoder_2e decoder_2e_2 (
    .in_1(in_2), .in_2(in_3), .in_3(in_1), .out_4(out_8), .out_5(out_9), .out_6(out_10), .out_7(out_11));
endmodule
