// Logisim project 1.3.1.3.circ as structural Verilog
module decoder_4 (
  input  in_1,
  input  in_2,
  input  in_3,
  input  in_4,
  output out_5,
  output out_6,
  output out_7,
  output out_8,
  output out_9,
  output out_10,
  output out_11,
  output out_12,
  output out_13,
  output out_14,
  output out_15,
  output out_16,
  output out_17,
  output out_18,
  output out_19,
  output out_20
);

  wire and_1_out, and_2_out, and_3_out, and_4_out;

  and and_1 (and_1_out, ~in_1, ~in_2);  // AND_Gate
  and and_2 (and_2_out, ~in_1, in_2);  // AND_Gate
  and and_3 (and_3_out, in_1, ~in_2);  // AND_Gate
  and and_4 (and_4_out, in_1, in_2);
  decoder_2e decoder_2e_1 (
    .in_1(in_3), .in_2(in_4), .in_3(and_1_out), .out_4(out_5), .out_5(out_6), .out_6(out_7), .out_7(out_8));
  decoder_2e decoder_2e_2 (
    .in_1(in_3), .in_2(in_4), .in_3(and_2_out), .out_4(out_9), .out_5(out_10), .out_6(out_11), .out_7(out_12));
  decoder_2e decoder_2e_3 (
    .in_1(in_3), .in_2(in_4), .in_3(and_3_out), .out_4(out_13), .out_5(out_14), .out_6(out_15), .out_7(out_16));
  decoder_2e decoder_2e_4 (
    .in_1(in_3), .in_2(in_4), .in_3(and_4_out), .out_4(out_17), .out_5(out_18), .out_6(out_19), .out_7(out_20));
endmodule
