// Logisim project 1.3.2.1.circ as structural Verilog: 2 circuits, main circuit main
module main (
  input  in_1,
  input  in_2,
  output out_3,
  output out_4
);

  half_adder half_adder_1 (.in_1(in_1), .in_2(in_2), .out_4(out_4), .out_3(out_3));
endmodule

module half_adder (
  input  in_1,
  input  in_2,
  output out_3,
  output out_4
);

  and and_1 (out_4, in_2, in_1);
  xor xor_1 (out_3, in_1, in_2);
endmodule
