// Logisim project 1.3.3.2.circ as structural Verilog: 3 circuits, main circuit main
module main (
  input  in_1,
  input  in_2,
  input  in_3,
  input  in_4,
  input  in_5,
  input  in_6,
  input  in_7,
  input  in_8,
  input  in_9,
  input  in_10,
  input  in_11,
  input  in_12,
  input  in_13,
  input  in_14,
  input  in_15,
  input  in_16,
  input  in_17,
  input  in_18,
  input  in_19,
  input  in_20,
  input  in_21,
  input  in_22,
  input  in_23,
  input  in_24,
  output out_25,
  output out_26,
  output out_27,
  output out_28,
  output out_29,
  output out_30,
  output out_31,
  output out_32,
  output out_33,
  output out_34,
  output out_35,
  output out_36,
  output out_37,
  output out_38
);

  _4_bit_adder u_4_bit_adder_1 (
    .in_2(in_1), .in_3(in_3), .in_4(in_5), .in_5(in_7), .in_6(in_10), .in_7(in_12), .in_8(in_14),
    .in_9(in_16), .in_1(1'b0), .out_14(out_32), .out_10(out_25), .out_11(out_26), .out_12(out_27),
    .out_13(out_29));
  _8_bit_adder u_8_bit_adder_1 (
    .in_1(in_2), .in_3(in_4), .in_4(in_6), .in_5(in_8), .in_6(in_9), .in_7(in_11), .in_8(in_13),
    .in_9(in_15), .in_10(in_17), .in_11(in_18), .in_12(in_19), .in_13(in_20), .in_14(in_21), .in_15(in_22),
    .in_16(in_23), .in_17(in_24), .in_2(1'b0), .out_26(out_38), .out_18(out_28), .out_19(out_30),
    .out_20(out_31), .out_21(out_33), .out_22(out_34), .out_23(out_35), .out_24(out_36), .out_25(out_37));
endmodule

module _4_bit_adder (
  input  in_1,
  input  in_2,
  input  in_3,
  input  in_4,
  input  in_5,
  input  in_6,
  input  in_7,
  input  in_8,
  input  in_9,
  output out_10,
  output out_11,
  output out_12,
  output out_13,
  output out_14
);

  wire full_adder_1_out_5, full_adder_2_out_5, full_adder_3_out_5;

  full_adder full_adder_1 (.in_2(in_6), .in_3(in_2), .in_1(in_1), .out_5(full_adder_1_out_5), .out_4(out_10));
  full_adder full_adder_2 (
    .in_2(in_7), .in_3(in_3), .in_1(full_adder_1_out_5), .out_5(full_adder_2_out_5), .out_4(out_11));
  full_adder full_adder_3 (
    .in_2(in_8), .in_3(in_4), .in_1(full_adder_2_out_5), .out_5(full_adder_3_out_5), .out_4(out_12));
  full_adder full_adder_4 (.in_2(in_9), .in_3(in_5), .in_1(full_adder_3_out_5), .out_5(out_14), .out_4(out_13));
endmodule

module _8_bit_adder (
  input  in_1,
  input  in_2,
  input  in_3,
  input  in_4,
  input  in_5,
  input  in_6,
  input  in_7,
  input  in_8,
  input  in_9,
  input  in_10,
  input  in_11,
  input  in_12,
  input  in_13,
  input  in_14,
  input  in_15,
  input  in_16,
  input  in_17,
  output out_18,
  output out_19,
  output out_20,
  output out_21,
  output out_22,
  output out_23,
  output out_24,
  output out_25,
  output out_26
);

  wire n4_bit_adder_1_out_14;

  _4_bit_adder u_4_bit_adder_1 (
    .in_2(in_1), .in_3(in_3), .in_4(in_4), .in_5(in_5), .in_6(in_10), .in_7(in_11), .in_8(in_12),
    .in_9(in_13), .in_1(in_2), .out_14(n4_bit_adder_1_out_14), .out_10(out_18), .out_11(out_19),
    .out_12(out_20), .out_13(out_21));
  _4_bit_adder u_4_bit_adder_2 (
    .in_2(in_6), .in_3(in_7), .in_4(in_8), .in_5(in_9), .in_6(in_14), .in_7(in_15), .in_8(in_16),
    .in_9(in_17), .in_1(n4_bit_adder_1_out_14), .out_14(out_26), .out_10(out_22), .out_11(out_23),
    .out_12(out_24), .out_13(out_25));
endmodule
