// Logisim project 1.4.2+3 bis.circ as structural Verilog: 1 circuit, main circuit main
module main (
  input  in_1,
  input  in_2,
  output out_3,
  output out_4,
  output out_5,
  output out_6
);

  wire and_1_out, clock_1_out, d_ff_1_q, d_ff_2_q, d_ff_3_q, d_ff_4_q, not_1_out, or_1_out;

  Clock clock_1 (.out(clock_1_out));
  not not_1 (not_1_out, in_1);
  D_Flip_Flop d_ff_1 (
    .clk(clock_1_out), .D(out_3), .Q(d_ff_1_q), .en(not_1_out), .reset(or_1_out));  // open: Qn, preset
  D_Flip_Flop d_ff_2 (
    .clk(clock_1_out), .D(out_4), .Q(d_ff_2_q), .preset(or_1_out), .en(not_1_out));  // open: Qn, reset
  increment increment_1 (
    .in_1(d_ff_1_q), .in_2(d_ff_2_q), .in_3(d_ff_3_q), .in_4(d_ff_4_q), .out_5(out_3), .out_6(out_4),
    .out_7(out_5), .out_8(out_6));
  and and_1 (and_1_out, d_ff_1_q, ~d_ff_2_q, d_ff_3_q, d_ff_4_q, not_1_out);  // AND_Gate
  D_Flip_Flop d_ff_3 (
    .clk(clock_1_out), .D(out_5), .Q(d_ff_3_q), .en(not_1_out), .reset(or_1_out));  // open: Qn, preset
  or or_1 (or_1_out, in_2, and_1_out);
  D_Flip_Flop d_ff_4 (
    .clk(clock_1_out), .D(out_6), .Q(d_ff_4_q), .en(not_1_out), .reset(or_1_out));  // open: Qn, preset
endmodule
