// Logisim project 1.4.2+3.circ as structural Verilog: 1 circuit, main circuit main
module main (
  input  in_1,
  input  in_2,
  output out_3,
  output out_4,
  output out_5,
  output out_6
);

  wire and_1_out, and_2_out, and_3_out, and_4_out, and_5_out, and_6_out, and_7_out, and_8_out, and_9_out,
       and_10_out, and_11_out, clock_1_out, d_ff_1_q, d_ff_2_q, d_ff_3_q, d_ff_4_q, increment_1_out_5,
       increment_1_out_6, increment_1_out_7, increment_1_out_8, or_1_out;

  Clock clock_1 (.out(clock_1_out));
  D_Flip_Flop d_ff_1 (.clk(clock_1_out), .D(out_3), .Q(d_ff_1_q));  // open: Qn, preset, en, reset
  D_Flip_Flop d_ff_2 (.clk(clock_1_out), .D(out_4), .Q(d_ff_2_q));  // open: Qn, preset, en, reset
  increment increment_1 (
    .in_1(d_ff_1_q), .in_2(d_ff_2_q), .in_3(d_ff_3_q), .in_4(d_ff_4_q), .out_5(increment_1_out_5),
    .out_6(increment_1_out_6), .out_7(increment_1_out_7), .out_8(increment_1_out_8));
  and and_1 (and_1_out, d_ff_1_q, ~d_ff_2_q, d_ff_3_q, d_ff_4_q, ~in_1);  // AND_Gate
  D_Flip_Flop d_ff_3 (.clk(clock_1_out), .D(out_5), .Q(d_ff_3_q));  // open: Qn, preset, en, reset
  and and_2 (and_2_out, ~in_1, ~and_1_out, ~in_2);  // AND_Gate
  and and_3 (and_3_out, in_1, ~in_2);  // AND_Gate
  D_Flip_Flop d_ff_4 (.clk(clock_1_out), .D(out_6), .Q(d_ff_4_q));  // open: Qn, preset, en, reset
  or or_1 (or_1_out, in_2, and_1_out);
  and and_4 (and_4_out, increment_1_out_5, and_2_out);
  and and_5 (and_5_out, increment_1_out_6, and_2_out);
  and and_6 (and_6_out, increment_1_out_7, and_2_out);
  and and_7 (and_7_out, increment_1_out_8, and_2_out);
  and and_8 (and_8_out, d_ff_1_q, and_3_out);
  and and_9 (and_9_out, d_ff_2_q, and_3_out);
  and and_10 (and_10_out, d_ff_3_q, and_3_out);
  and and_11 (and_11_out, d_ff_4_q, and_3_out);
  or or_2 (out_3, and_4_out, or_1_out, and_8_out);
  or or_3 (out_4, and_5_out, or_1_out, and_9_out);
  or or_4 (out_5, and_6_out, and_10_out);
  or or_5 (out_6, and_7_out, and_11_out);
endmodule
