// Logisim project 1.5.2.circ as structural Verilog: 1 circuit, main circuit main
module main (
  input  in_1,
  input  in_2,
  output out_3,
  output out_4
);

  wire and_3_out, and_4_out, and_5_out, and_6_out, and_7_out, and_8_out, and_9_out, and_10_out, clock_1_out,
       d_ff_1_q, d_ff_2_q, d_ff_3_q, or_1_out, or_2_out, or_3_out;

  Clock clock_1 (.out(clock_1_out));
  D_Flip_Flop d_ff_1 (.clk(clock_1_out), .D(or_3_out), .Q(d_ff_1_q));  // open: Qn, preset, en, reset
  D_Flip_Flop d_ff_2 (.clk(clock_1_out), .D(or_2_out), .Q(d_ff_2_q));  // open: Qn, preset, en, reset
  D_Flip_Flop d_ff_3 (.clk(clock_1_out), .D(or_1_out), .Q(d_ff_3_q));  // open: Qn, preset, en, reset
  and and_1 (out_3, ~d_ff_1_q, d_ff_2_q, d_ff_3_q);  // AND_Gate
  and and_2 (out_4, ~d_ff_1_q, ~d_ff_2_q, ~d_ff_3_q);  // AND_Gate
  and and_3 (and_3_out, d_ff_1_q, ~d_ff_2_q, ~d_ff_3_q);  // AND_Gate
  and and_4 (and_4_out, ~d_ff_1_q, d_ff_2_q, d_ff_3_q, in_2);  // AND_Gate
  and and_5 (and_5_out, ~d_ff_1_q, ~d_ff_2_q, d_ff_3_q);  // AND_Gate
  and and_6 (and_6_out, ~d_ff_1_q, d_ff_2_q, ~d_ff_3_q);  // AND_Gate
  and and_7 (and_7_out, ~d_ff_1_q, d_ff_2_q, d_ff_3_q, ~in_2);  // AND_Gate
  and and_8 (and_8_out, ~d_ff_1_q, ~d_ff_2_q, ~d_ff_3_q, in_1);  // AND_Gate
  and and_9 (and_9_out, ~d_ff_1_q, d_ff_2_q, ~d_ff_3_q);  // AND_Gate
  and and_10 (and_10_out, d_ff_1_q, ~d_ff_2_q, ~d_ff_3_q);  // AND_Gate
  or or_1 (or_1_out, and_10_out, and_7_out, and_9_out, and_8_out);
  or or_2 (or_2_out, and_7_out, and_6_out, and_5_out);
  or or_3 (or_3_out, and_4_out, and_3_out);
endmodule
