// Logisim project 1.5.3.circ as structural Verilog: 1 circuit, main circuit main
module main (
  input  in_1,
  input  in_2,
  output out_3,
  output out_4,
  output out_5,
  output out_6,
  output out_7
);

  wire clock_1_out, d_ff_1_q, d_ff_2_q, d_ff_3_q, d_ff_4_q, d_ff_5_q;

  Clock clock_1 (.out(clock_1_out));
  D_Flip_Flop d_ff_1 (.clk(clock_1_out), .D(out_3), .Q(d_ff_1_q), .en(in_1));  // open: Qn, preset, reset
  D_Flip_Flop d_ff_2 (.clk(clock_1_out), .D(out_4), .Q(d_ff_2_q), .en(in_1));  // open: Qn, preset, reset
  D_Flip_Flop d_ff_3 (.clk(clock_1_out), .D(out_5), .Q(d_ff_3_q), .en(in_1));  // open: Qn, preset, reset
  D_Flip_Flop d_ff_4 (.clk(clock_1_out), .D(out_6), .Q(d_ff_4_q), .en(in_1));  // open: Qn, preset, reset
  D_Flip_Flop d_ff_5 (.clk(clock_1_out), .D(in_2), .Q(d_ff_5_q), .en(in_1));  // open: Qn, preset, reset
  _4_bit_adder u_4_bit_adder_1 (
    .in_2(d_ff_1_q), .in_3(d_ff_2_q), .in_4(d_ff_3_q), .in_5(d_ff_4_q), .in_6(1'b1), .in_7(d_ff_5_q),
    .in_8(d_ff_5_q), .in_9(d_ff_5_q), .in_1(1'b0), .out_14(out_7), .out_10(out_3), .out_11(out_4),
    .out_12(out_5), .out_13(out_6));
endmodule
