// Logisim project 1.6.2.circ as structural Verilog: 1 circuit, main circuit main
module main (
  input  in_1,
  input  in_2,
  input  in_3,
  input  in_4,
  input  in_5,
  input  in_6,
  output out_7,
  output out_8,
  output out_9,
  output out_10,
  output out_11,
  output out_12
);

  wire and_2_out, and_3_out, and_4_out, and_5_out, and_6_out, and_7_out, and_8_out, and_9_out,
       full_adder_1_out_4, full_adder_1_out_5, full_adder_2_out_5, half_adder_1_out_4, half_adder_2_out_3,
       half_adder_2_out_4, half_adder_3_out_4;

  and and_1 (out_7, in_1, in_4);
  and and_2 (and_2_out, in_2, in_4);
  and and_3 (and_3_out, in_3, in_4);
  and and_4 (and_4_out, in_1, in_5);
  and and_5 (and_5_out, in_2, in_5);
  and and_6 (and_6_out, in_3, in_5);
  and and_7 (and_7_out, in_1, in_6);
  and and_8 (and_8_out, in_2, in_6);
  and and_9 (and_9_out, in_3, in_6);
  half_adder half_adder_1 (.in_1(and_2_out), .in_2(and_4_out), .out_4(half_adder_1_out_4), .out_3(out_8));
  full_adder full_adder_1 (
    .in_2(and_3_out), .in_3(and_5_out), .in_1(half_adder_1_out_4), .out_5(full_adder_1_out_5),
    .out_4(full_adder_1_out_4));
  half_adder half_adder_2 (
    .in_1(full_adder_1_out_5), .in_2(and_6_out), .out_4(half_adder_2_out_4), .out_3(half_adder_2_out_3));
  half_adder half_adder_3 (.in_1(full_adder_1_out_4), .in_2(and_7_out), .out_4(half_adder_3_out_4), .out_3(out_9));
  full_adder full_adder_2 (
    .in_2(half_adder_2_out_3), .in_3(and_8_out), .in_1(half_adder_3_out_4), .out_5(full_adder_2_out_5),
    .out_4(out_10));
  full_adder full_adder_3 (
    .in_2(and_9_out), .in_3(half_adder_2_out_4), .in_1(full_adder_2_out_5), .out_5(out_12), .out_4(out_11));
endmodule
