// Logisim project 1.7.2.circ as structural Verilog: 1 circuit, main circuit main
module main (
  input  in_1,
  output out_2,
  output out_3
);

  wire and_1_out, clock_1_out;

  Clock clock_1 (.out(clock_1_out));
  and and_1 (and_1_out, clock_1_out, in_1);
  D_Flip_Flop d_ff_1 (.clk(and_1_out), .D(out_3), .Q(out_2), .Qn(out_3));  // open: preset, en, reset
endmodule
