// Logisim project 1.3.1.1.circ as structural Verilog: 2 circuits, main circuit main
module main (
  input  in_1,
  input  in_2,
  input  in_3,
  output out_4,
  output out_5,
  output out_6,
  output out_7
);

  decoder_2e decoder_2e_1 (
    .in_1(in_1), .in_2(in_2), .in_3(in_3), .out_4(out_4), .out_5(out_5), .out_6(out_6), .out_7(out_7));
endmodule

module decoder_2e (
  input  in_1,
  input  in_2,
  input  in_3,
  output out_4,
  output out_5,
  output out_6,
  output out_7
);

  and and_1 (out_4, ~in_1, in_3, ~in_2);  // AND_Gate
  and and_2 (out_5, ~in_1, in_3, in_2);  // AND_Gate
  and and_3 (out_6, in_1, in_3, ~in_2);  // AND_Gate
  and and_4 (out_7, in_1, in_3, in_2);
endmodule
