// Logisim project 1.3.1.3.circ as structural Verilog: 3 circuits, main circuit main
module main (
  input  in_1,
  input  in_2,
  input  in_3,
  input  in_4,
  input  in_5,
  input  in_6,
  input  in_7,
  input  in_8,
  input  in_9,
  output out_10,
  output out_11,
  output out_12,
  output out_13,
  output out_14,
  output out_15,
  output out_16,
  output out_17,
  output out_18,
  output out_19,
  output out_20,
  output out_21,
  output out_22,
  output out_23,
  output out_24,
  output out_25,
  output out_26,
  output out_27,
  output out_28,
  output out_29,
  output out_30,
  output out_31,
  output out_32,
  output out_33,
  output out_34,
  output out_35,
  output out_36,
  output out_37,
  output out_38,
  output out_39,
  output out_40,
  output out_41
);

  decoder_4 decoder_4_1 (
    .in_1(in_1), .in_2(in_3), .in_3(in_5), .in_4(in_7), .out_5(out_10), .out_6(out_12), .out_7(out_14),
    .out_8(out_16), .out_9(out_18), .out_10(out_20), .out_11(out_22), .out_12(out_24), .out_13(out_26),
    .out_14(out_28), .out_15(out_30), .out_16(out_32), .out_17(out_34), .out_18(out_36), .out_19(out_38),
    .out_20(out_40));
  decoder_4e decoder_4e_1 (
    .in_1(in_2), .in_2(in_4), .in_3(in_6), .in_4(in_8), .in_5(in_9), .out_6(out_11), .out_7(out_13),
    .out_8(out_15), .out_9(out_17), .out_10(out_19), .out_11(out_21), .out_12(out_23), .out_13(out_25),
    .out_14(out_27), .out_15(out_29), .out_16(out_31), .out_17(out_33), .out_18(out_35), .out_19(out_37),
    .out_20(out_39), .out_21(out_41));
endmodule

module decoder_4 (
  input  in_1,
  input  in_2,
  input  in_3,
  input  in_4,
  output out_5,
  output out_6,
  output out_7,
  output out_8,
  output out_9,
  output out_10,
  output out_11,
  output out_12,
  output out_13,
  output out_14,
  output out_15,
  output out_16,
  output out_17,
  output out_18,
  output out_19,
  output out_20
);

  wire and_1_out, and_2_out, and_3_out, and_4_out;

  and and_1 (and_1_out, ~in_1, ~in_2);  // AND_Gate
  and and_2 (and_2_out, ~in_1, in_2);  // AND_Gate
  and and_3 (and_3_out, in_1, ~in_2);  // AND_Gate
  and and_4 (and_4_out, in_1, in_2);
  decoder_2e decoder_2e_1 (
    .in_1(in_3), .in_2(in_4), .in_3(and_1_out), .out_4(out_5), .out_5(out_6), .out_6(out_7), .out_7(out_8));
  decoder_2e decoder_2e_2 (
    .in_1(in_3), .in_2(in_4), .in_3(and_2_out), .out_4(out_9), .out_5(out_10), .out_6(out_11), .out_7(out_12));
  decoder_2e decoder_2e_3 (
    .in_1(in_3), .in_2(in_4), .in_3(and_3_out), .out_4(out_13), .out_5(out_14), .out_6(out_15), .out_7(out_16));
  decoder_2e decoder_2e_4 (
    .in_1(in_3), .in_2(in_4), .in_3(and_4_out), .out_4(out_17), .out_5(out_18), .out_6(out_19), .out_7(out_20));
endmodule

module decoder_4e (
  input  in_1,
  input  in_2,
  input  in_3,
  input  in_4,
  input  in_5,
  output out_6,
  output out_7,
  output out_8,
  output out_9,
  output out_10,
  output out_11,
  output out_12,
  output out_13,
  output out_14,
  output out_15,
  output out_16,
  output out_17,
  output out_18,
  output out_19,
  output out_20,
  output out_21
);

  wire decoder_2e_1_out_4, decoder_2e_1_out_5, decoder_2e_1_out_6, decoder_2e_1_out_7;

  decoder_2e decoder_2e_1 (
    .in_1(in_1), .in_2(in_2), .in_3(in_5), .out_4(decoder_2e_1_out_4), .out_5(decoder_2e_1_out_5),
    .out_6(decoder_2e_1_out_6), .out_7(decoder_2e_1_out_7));
  decoder_2e decoder_2e_2 (
    .in_1(in_3), .in_2(in_4), .in_3(decoder_2e_1_out_4), .out_4(out_6), .out_5(out_7), .out_6(out_8),
    .out_7(out_9));
  decoder_2e decoder_2e_3 (
    .in_1(in_3), .in_2(in_4), .in_3(decoder_2e_1_out_5), .out_4(out_10), .out_5(out_11), .out_6(out_12),
    .out_7(out_13));
  decoder_2e decoder_2e_4 (
    .in_1(in_3), .in_2(in_4), .in_3(decoder_2e_1_out_6), .out_4(out_14), .out_5(out_15), .out_6(out_16),
    .out_7(out_17));
  decoder_2e decoder_2e_5 (
    .in_1(in_3), .in_2(in_4), .in_3(decoder_2e_1_out_7), .out_4(out_18), .out_5(out_19), .out_6(out_20),
    .out_7(out_21));
endmodule
