// Logisim project 1.3.2.2.circ as structural Verilog: 2 circuits, main circuit main
module main (
  input  in_1,
  input  in_2,
  input  in_3,
  input  in_4,
  output out_5,
  output out_6,
  output out_7,
  output out_8
);

  increment increment_1 (
    .in_1(in_1), .in_2(in_2), .in_3(in_3), .in_4(in_4), .out_5(out_5), .out_6(out_6), .out_7(out_7),
    .out_8(out_8));
endmodule

module increment (
  input  in_1,
  input  in_2,
  input  in_3,
  input  in_4,
  output out_5,
  output out_6,
  output out_7,
  output out_8
);

  wire half_adder_1_out_4, half_adder_2_out_4, half_adder_3_out_4;

  half_adder half_adder_1 (.in_1(1'b1), .in_2(in_1), .out_4(half_adder_1_out_4), .out_3(out_5));
  half_adder half_adder_2 (.in_1(half_adder_1_out_4), .in_2(in_2), .out_4(half_adder_2_out_4), .out_3(out_6));
  half_adder half_adder_3 (.in_1(half_adder_2_out_4), .in_2(in_3), .out_4(half_adder_3_out_4), .out_3(out_7));
  half_adder half_adder_4 (.in_1(half_adder_3_out_4), .in_2(in_4), .out_3(out_8));  // open: out_4
endmodule
