// Logisim project 1.6.3.circ as structural Verilog: 1 circuit, main circuit main
module main (
  output out_1,
  output out_2
);

  wire _0_out, _1_out, and_3_out, and_4_out, and_5_out, and_6_out, and_7_out, and_8_out, and_9_out,
       and_10_out, clock_1_out, d_ff_1_q, d_ff_2_q, d_ff_3_q, d_ff_4_q, d_ff_5_q, nor_1_out, or_1_out,
       or_2_out, or_3_out;

  LED led_1 (.in(d_ff_1_q));
  Button _1 (.out(_1_out));
  LED led_2 (.in(d_ff_2_q));
  Button _0 (.out(_0_out));
  nor nor_1 (nor_1_out, out_2, out_1);
  LED moving (.in(nor_1_out));
  Clock clock_1 (.out(clock_1_out));
  D_Flip_Flop d_ff_1 (.clk(_1_out), .D(_1_out), .Q(d_ff_1_q), .reset(out_1));  // open: Qn, preset, en
  D_Flip_Flop d_ff_2 (.clk(_0_out), .D(_0_out), .Q(d_ff_2_q), .reset(out_2));  // open: Qn, preset, en
  D_Flip_Flop d_ff_3 (.clk(clock_1_out), .D(or_3_out), .Q(d_ff_3_q));  // open: Qn, preset, en, reset
  D_Flip_Flop d_ff_4 (.clk(clock_1_out), .D(or_2_out), .Q(d_ff_4_q));  // open: Qn, preset, en, reset
  D_Flip_Flop d_ff_5 (.clk(clock_1_out), .D(or_1_out), .Q(d_ff_5_q));  // open: Qn, preset, en, reset
  and and_1 (out_1, ~d_ff_3_q, d_ff_4_q, d_ff_5_q);  // AND_Gate
  and and_2 (out_2, ~d_ff_3_q, ~d_ff_4_q, ~d_ff_5_q);  // AND_Gate
  and and_3 (and_3_out, d_ff_3_q, ~d_ff_4_q, ~d_ff_5_q);  // AND_Gate
  and and_4 (and_4_out, ~d_ff_3_q, d_ff_4_q, d_ff_5_q, d_ff_2_q);  // AND_Gate
  and and_5 (and_5_out, ~d_ff_3_q, ~d_ff_4_q, d_ff_5_q);  // AND_Gate
  and and_6 (and_6_out, ~d_ff_3_q, d_ff_4_q, ~d_ff_5_q);  // AND_Gate
  and and_7 (and_7_out, ~d_ff_3_q, d_ff_4_q, d_ff_5_q, ~d_ff_2_q);  // AND_Gate
  and and_8 (and_8_out, ~d_ff_3_q, ~d_ff_4_q, ~d_ff_5_q, d_ff_1_q);  // AND_Gate
  and and_9 (and_9_out, ~d_ff_3_q, d_ff_4_q, ~d_ff_5_q);  // AND_Gate
  and and_10 (and_10_out, d_ff_3_q, ~d_ff_4_q, ~d_ff_5_q);  // AND_Gate
  or or_1 (or_1_out, and_10_out, and_7_out, and_9_out, and_8_out);
  or or_2 (or_2_out, and_7_out, and_6_out, and_5_out);
  or or_3 (or_3_out, and_4_out, and_3_out);
  LED led_3 (.in(out_1));
  LED led_4 (.in(out_2));
endmodule
