// Logisim project ESERCIZIO2.1.circ as structural Verilog: 1 circuit, main circuit main
module main (
  input  in_1,
  input  in_2,
  input  in_3,
  input  in_4,
  output out_5
);

  wire and_1_out, and_2_out, and_3_out, and_4_out, not_1_out, not_2_out, not_3_out, not_4_out, not_5_out;

  not not_1 (not_1_out, in_1);
  not not_2 (not_2_out, in_2);
  not not_3 (not_3_out, in_2);
  not not_4 (not_4_out, in_1);
  not not_5 (not_5_out, in_3);
  and and_1 (and_1_out, not_1_out, not_2_out, in_3);
  and and_2 (and_2_out, not_3_out, in_3, in_4);
  and and_3 (and_3_out, not_4_out, in_2, in_4);
  and and_4 (and_4_out, in_2, not_5_out, in_4);
  or or_1 (out_5, and_1_out, and_2_out, and_3_out, and_4_out);

  // Notes on the sheet:
  //   a
  //   b
  //   ABCD
  //   0010 = 2
  //   0 se non lo rappresentano
  //   c
  //   d
  //   output: 1 se i 4 bit rappresentano un numero primo
  //   input: 4x1bit
  //   ESERCIZIO 2.1
endmodule
