// Logisim project ESERCIZIO2.3.2.circ as structural Verilog: 3 circuits, main circuit main
module main (
  input  in_1,
  input  in_2,
  input  in_3,
  output out_4
);

  MULTIPLEXER multiplexer_1 (.in_1(in_1), .in_2(in_2), .in_3(in_3), .out_4(out_4));

  // Notes on the sheet:
  //   usa 3 multiplexer "MULTIPLEXER" PER CREARE 1 multiplexer a 2 input control
endmodule

module MULTIPLEXER (
  input  in_1,
  input  in_2,
  input  in_3,
  output out_4
);

  wire and_1_out, and_2_out;

  and and_1 (and_1_out, in_1, ~in_3);  // AND_Gate
  and and_2 (and_2_out, in_3, in_2);
  or or_1 (out_4, and_1_out, and_2_out);

  // Notes on the sheet:
  //   fai un multiplexer con 1 ingresso di controllo
  //   ESERCIZIO 2.3.1
endmodule

module MULTIPLEXER2Input (
  input  in_1,
  input  in_2,
  input  in_3,
  input  in_4,
  input  in_5,
  input  in_6,
  output out_7
);

  wire multiplexer_1_out_4, multiplexer_2_out_4;

  MULTIPLEXER multiplexer_1 (.in_1(in_1), .in_2(in_2), .in_3(in_5), .out_4(multiplexer_1_out_4));
  MULTIPLEXER multiplexer_2 (.in_1(in_3), .in_2(in_4), .in_3(in_5), .out_4(multiplexer_2_out_4));
  MULTIPLEXER multiplexer_3 (.in_1(multiplexer_1_out_4), .in_2(multiplexer_2_out_4), .in_3(in_6), .out_4(out_7));

  // Notes on the sheet:
  //   usa 3 multiplexer "MULTIPLEXER" PER CREARE 1 multiplexer a 2 input control
endmodule
