// Logisim project ESERCIZIO3.1.1-3.1.3.circ as structural Verilog: 4 circuits, main circuit main
module main (
);


  // Notes on the sheet:
  //   ESERCIZIO 3.1.1
endmodule

module Decoder2Input (
  input  in_1,
  input  in_2,
  input  in_3,
  output out_4,
  output out_5,
  output out_6,
  output out_7
);

  and and_1 (out_4, ~in_2, in_3, ~in_1);  // AND_Gate
  and and_2 (out_5, in_2, in_3, ~in_1);  // AND_Gate
  and and_3 (out_6, ~in_2, in_3, in_1);  // AND_Gate
  and and_4 (out_7, in_2, in_3, in_1);

  // Notes on the sheet:
  //   esercizio 3.1.1
endmodule

module Decoder3Input (
  input  in_1,
  input  in_2,
  input  in_3,
  output out_4,
  output out_5,
  output out_6,
  output out_7,
  output out_8,
  output out_9,
  output out_10,
  output out_11
);

  wire not_1_out;

  not not_1 (not_1_out, in_1);
  Decoder2Input decoder2input_1 (
    .in_1(in_2), .in_2(in_3), .in_3(not_1_out), .out_4(out_4), .out_5(out_5), .out_6(out_6), .out_7(out_7));
  Decoder2Input decoder2input_2 (
    .in_1(in_2), .in_2(in_3), .in_3(in_1), .out_4(out_8), .out_5(out_9), .out_6(out_10), .out_7(out_11));
endmodule

module Decoder4Input (
  input  in_1,
  input  in_2,
  input  in_3,
  input  in_4,
  input  in_5,
  output out_6,
  output out_7,
  output out_8,
  output out_9,
  output out_10,
  output out_11,
  output out_12,
  output out_13,
  output out_14,
  output out_15,
  output out_16,
  output out_17,
  output out_18,
  output out_19,
  output out_20,
  output out_21
);

  wire decoder2input_1_out_4, decoder2input_1_out_5, decoder2input_1_out_6, decoder2input_1_out_7;

  Decoder2Input decoder2input_1 (
    .in_1(in_1), .in_2(in_2), .in_3(in_5), .out_4(decoder2input_1_out_4), .out_5(decoder2input_1_out_5),
    .out_6(decoder2input_1_out_6), .out_7(decoder2input_1_out_7));
  Decoder2Input decoder2input_2 (
    .in_1(in_3), .in_2(in_4), .in_3(decoder2input_1_out_4), .out_4(out_6), .out_5(out_7), .out_6(out_8),
    .out_7(out_9));
  Decoder2Input decoder2input_3 (
    .in_1(in_3), .in_2(in_4), .in_3(decoder2input_1_out_5), .out_4(out_10), .out_5(out_11), .out_6(out_12),
    .out_7(out_13));
  Decoder2Input decoder2input_4 (
    .in_1(in_3), .in_2(in_4), .in_3(decoder2input_1_out_6), .out_4(out_14), .out_5(out_15), .out_6(out_16),
    .out_7(out_17));
  Decoder2Input decoder2input_5 (
    .in_1(in_3), .in_2(in_4), .in_3(decoder2input_1_out_7), .out_4(out_18), .out_5(out_19), .out_6(out_20),
    .out_7(out_21));
endmodule
