// Logisim project ESERCIZIO3.2.1-3.3.2&4.1-4.3.circ as structural Verilog
module haldAdder (
  input  in_1,
  input  in_2,
  output out_3,
  output out_4
);

  and and_1 (out_4, in_2, in_1);
  xor xor_1 (out_3, in_1, in_2);

  // Notes on the sheet:
  //   ESERCIZIO 2.3.1
endmodule

module ADDER4Input (
  input  in_1,
  input  in_2,
  input  in_3,
  input  in_4,
  output out_5,
  output out_6,
  output out_7,
  output out_8,
  output out_9
);

  wire haldadder_1_out_4, haldadder_2_out_4, haldadder_3_out_4;

  haldAdder haldadder_1 (.in_1(in_4), .in_2(1'b1), .out_4(haldadder_1_out_4), .out_3(out_9));
  haldAdder haldadder_2 (.in_1(haldadder_1_out_4), .in_2(in_3), .out_4(haldadder_2_out_4), .out_3(out_8));
  haldAdder haldadder_3 (.in_1(haldadder_2_out_4), .in_2(in_2), .out_4(haldadder_3_out_4), .out_3(out_7));
  haldAdder haldadder_4 (.in_1(haldadder_3_out_4), .in_2(in_1), .out_4(out_5), .out_3(out_6));

  // Notes on the sheet:
  //   ESERCIZIO 3.2.2
endmodule

module FULL_ADDER (
  input  in_1,
  input  in_2,
  input  in_3,
  output out_4,
  output out_5
);

  wire haldadder_1_out_3, haldadder_1_out_4, haldadder_2_out_4;

  haldAdder haldadder_1 (.in_1(in_3), .in_2(in_2), .out_4(haldadder_1_out_4), .out_3(haldadder_1_out_3));
  or or_1 (out_5, haldadder_1_out_4, haldadder_2_out_4);
  haldAdder haldadder_2 (.in_1(haldadder_1_out_3), .in_2(in_1), .out_4(haldadder_2_out_4), .out_3(out_4));

  // Notes on the sheet:
  //   ESERCIZIO 3.3.1
endmodule

module SOMMA4INPUT (
  input  in_1,
  input  in_2,
  input  in_3,
  input  in_4,
  input  in_5,
  input  in_6,
  input  in_7,
  input  in_8,
  output out_9,
  output out_10,
  output out_11,
  output out_12,
  output out_13
);

  wire full_adder_1_out_5, full_adder_2_out_5, full_adder_3_out_5;

  FULL_ADDER full_adder_1 (.in_2(in_4), .in_3(in_8), .in_1(1'b0), .out_4(out_13), .out_5(full_adder_1_out_5));
  FULL_ADDER full_adder_2 (
    .in_2(in_3), .in_3(in_7), .in_1(full_adder_1_out_5), .out_4(out_12), .out_5(full_adder_2_out_5));
  FULL_ADDER full_adder_3 (
    .in_2(in_2), .in_3(in_6), .in_1(full_adder_2_out_5), .out_4(out_11), .out_5(full_adder_3_out_5));
  FULL_ADDER full_adder_4 (.in_2(in_1), .in_3(in_5), .in_1(full_adder_3_out_5), .out_4(out_10), .out_5(out_9));

  // Notes on the sheet:
  //   somma tra 2 stringhe di 4 bit con FULL ADDER
  //   esercizio 3.3.2
endmodule

module contatoreSequenziale (
);

  wire adder4input_1_out_6, adder4input_1_out_7, adder4input_1_out_8, adder4input_1_out_9, clock_1_out,
       d_ff_1_q, d_ff_2_q, d_ff_3_q, d_ff_4_q;

  Clock clock_1 (.out(clock_1_out));
  ADDER4Input adder4input_1 (
    .in_1(d_ff_1_q), .in_2(d_ff_2_q), .in_3(d_ff_3_q), .in_4(d_ff_4_q), .out_6(adder4input_1_out_6),
    .out_7(adder4input_1_out_7), .out_8(adder4input_1_out_8), .out_9(adder4input_1_out_9));  // open: out_5
  D_Flip_Flop d_ff_1 (.clk(clock_1_out), .D(adder4input_1_out_6), .Q(d_ff_1_q));  // open: Qn, preset, en, reset
  D_Flip_Flop d_ff_2 (.clk(clock_1_out), .D(adder4input_1_out_7), .Q(d_ff_2_q));  // open: Qn, preset, en, reset
  D_Flip_Flop d_ff_3 (.clk(clock_1_out), .D(adder4input_1_out_8), .Q(d_ff_3_q));  // open: Qn, preset, en, reset
  D_Flip_Flop d_ff_4 (.clk(clock_1_out), .D(adder4input_1_out_9), .Q(d_ff_4_q));  // open: Qn, preset, en, reset
endmodule

module _4_2 (
  input  in_1,
  input  r
);

  wire adder4input_1_out_6, adder4input_1_out_7, adder4input_1_out_8, adder4input_1_out_9, clock_1_out,
       d_ff_1_q, d_ff_2_q, d_ff_3_q, d_ff_4_q, not_1_out;

  Clock clock_1 (.out(clock_1_out));
  not not_1 (not_1_out, in_1);
  ADDER4Input adder4input_1 (
    .in_1(d_ff_1_q), .in_2(d_ff_2_q), .in_3(d_ff_3_q), .in_4(d_ff_4_q), .out_6(adder4input_1_out_6),
    .out_7(adder4input_1_out_7), .out_8(adder4input_1_out_8), .out_9(adder4input_1_out_9));  // open: out_5
  D_Flip_Flop d_ff_1 (
    .clk(clock_1_out), .D(adder4input_1_out_6), .Q(d_ff_1_q), .en(not_1_out), .reset(r));  // open: Qn, preset
  D_Flip_Flop d_ff_2 (
    .clk(clock_1_out), .D(adder4input_1_out_7), .Q(d_ff_2_q), .en(not_1_out), .reset(r));  // open: Qn, preset
  D_Flip_Flop d_ff_3 (
    .clk(clock_1_out), .D(adder4input_1_out_8), .Q(d_ff_3_q), .preset(r), .en(not_1_out));  // open: Qn, reset
  D_Flip_Flop d_ff_4 (
    .clk(clock_1_out), .D(adder4input_1_out_9), .Q(d_ff_4_q), .preset(r), .en(not_1_out));  // open: Qn, reset

  // Notes on the sheet:
  //   S
endmodule

module _4_3 (
  input  r,
  input  in_2
);

  wire adder4input_1_out_6, adder4input_1_out_7, adder4input_1_out_8, adder4input_1_out_9, and_1_out,
       clock_1_out, d_ff_1_q, d_ff_2_q, d_ff_3_q, d_ff_3_qn, d_ff_4_q, not_1_out, or_1_out;

  Clock clock_1 (.out(clock_1_out));
  not not_1 (not_1_out, in_2);
  ADDER4Input adder4input_1 (
    .in_1(d_ff_1_q), .in_2(d_ff_2_q), .in_3(d_ff_3_q), .in_4(d_ff_4_q), .out_6(adder4input_1_out_6),
    .out_7(adder4input_1_out_7), .out_8(adder4input_1_out_8), .out_9(adder4input_1_out_9));  // open: out_5
  D_Flip_Flop d_ff_1 (
    .clk(clock_1_out), .D(adder4input_1_out_6), .Q(d_ff_1_q), .en(not_1_out), .reset(or_1_out));  // open: Qn, preset
  D_Flip_Flop d_ff_2 (
    .clk(clock_1_out), .D(adder4input_1_out_7), .Q(d_ff_2_q), .en(not_1_out), .reset(or_1_out));  // open: Qn, preset
  D_Flip_Flop d_ff_3 (
    .clk(clock_1_out), .D(adder4input_1_out_8), .Q(d_ff_3_q), .Qn(d_ff_3_qn), .preset(or_1_out),
    .en(not_1_out));  // open: reset
  D_Flip_Flop d_ff_4 (
    .clk(clock_1_out), .D(adder4input_1_out_9), .Q(d_ff_4_q), .preset(or_1_out), .en(not_1_out));  // open: Qn, reset
  or or_1 (or_1_out, r, and_1_out);
  and and_1 (and_1_out, d_ff_1_q, d_ff_2_q, d_ff_3_qn, d_ff_4_q);

  // Notes on the sheet:
  //   quando arrivo a 12 (1101) torno a contare da 3 (0011)
  //   S
endmodule
