// Logisim project 3.circ as structural Verilog: 7 circuits, main circuit 2
module SILVIO (
  input  in_1,
  input  in_2,
  input  in_3,
  output out_4,
  output out_5,
  output out_6,
  output out_7
);

  and and_1 (out_4, ~in_2, ~in_3, in_1);  // AND_Gate
  and and_2 (out_5, ~in_2, in_3, in_1);  // AND_Gate
  and and_3 (out_6, in_2, ~in_3, in_1);  // AND_Gate
  and and_4 (out_7, in_2, in_3, in_1);
endmodule

module _2 (
  input  in_1,
  input  in_2,
  input  in_3,
  input  in_4,
  input  in_5,
  output out_6,
  output out_7,
  output out_8,
  output out_9,
  output out_10,
  output out_11,
  output out_12,
  output out_13,
  output out_14,
  output out_15,
  output out_16,
  output out_17,
  output out_18,
  output out_19,
  output out_20,
  output out_21
);

  wire silvio_5_out_4, silvio_5_out_5, silvio_5_out_6, silvio_5_out_7;

  SILVIO silvio_1 (
    .in_1(silvio_5_out_7), .in_2(in_1), .in_3(in_2), .out_4(out_6), .out_5(out_7), .out_6(out_8),
    .out_7(out_9));
  SILVIO silvio_2 (
    .in_1(silvio_5_out_6), .in_2(in_1), .in_3(in_2), .out_4(out_10), .out_5(out_11), .out_6(out_12),
    .out_7(out_13));
  SILVIO silvio_3 (
    .in_1(silvio_5_out_5), .in_2(in_1), .in_3(in_2), .out_4(out_14), .out_5(out_15), .out_6(out_16),
    .out_7(out_17));
  SILVIO silvio_4 (
    .in_1(silvio_5_out_4), .in_2(in_1), .in_3(in_2), .out_4(out_18), .out_5(out_19), .out_6(out_20),
    .out_7(out_21));
  SILVIO silvio_5 (
    .in_1(in_5), .in_2(in_3), .in_3(in_4), .out_4(silvio_5_out_4), .out_5(silvio_5_out_5),
    .out_6(silvio_5_out_6), .out_7(silvio_5_out_7));
endmodule

module _1 (
  input  in_1,
  input  in_2,
  input  in_3,
  output out_4,
  output out_5,
  output out_6,
  output out_7,
  output out_8,
  output out_9,
  output out_10,
  output out_11
);

  wire not_1_out;

  not not_1 (not_1_out, in_3);
  SILVIO silvio_1 (
    .in_1(not_1_out), .in_2(in_1), .in_3(in_2), .out_4(out_4), .out_5(out_5), .out_6(out_6), .out_7(out_7));
  SILVIO silvio_2 (.in_1(in_3), .in_2(in_1), .in_3(in_2), .out_4(out_8), .out_5(out_9), .out_6(out_10), .out_7(out_11));
endmodule

module halfAdder (
  input  in_1,
  input  in_2,
  output out_3,
  output out_4
);

  and and_1 (out_4, in_1, in_2);
  xor xor_1 (out_3, in_1, in_2);
endmodule

module fullAdder (
  input  in_1,
  input  in_2,
  input  in_3,
  output out_4,
  output out_5
);

  wire halfadder_1_out_4, halfadder_2_out_3, halfadder_2_out_4;

  halfAdder halfadder_1 (.in_1(in_1), .in_2(halfadder_2_out_3), .out_3(out_4), .out_4(halfadder_1_out_4));
  halfAdder halfadder_2 (.in_1(in_2), .in_2(in_3), .out_3(halfadder_2_out_3), .out_4(halfadder_2_out_4));
  or or_1 (out_5, halfadder_1_out_4, halfadder_2_out_4);
endmodule

module _4 (
  input  in_1,
  input  in_2,
  input  in_3,
  input  in_4,
  output out_5,
  output out_6,
  output out_7,
  output out_8,
  output out_9
);

  wire halfadder_1_out_4, halfadder_2_out_4, halfadder_3_out_4;

  halfAdder halfadder_1 (.in_1(1'b1), .in_2(in_4), .out_3(out_9), .out_4(halfadder_1_out_4));
  halfAdder halfadder_2 (.in_1(halfadder_1_out_4), .in_2(in_3), .out_3(out_8), .out_4(halfadder_2_out_4));
  halfAdder halfadder_3 (.in_1(halfadder_2_out_4), .in_2(in_2), .out_3(out_7), .out_4(halfadder_3_out_4));
  halfAdder halfadder_4 (.in_1(halfadder_3_out_4), .in_2(in_1), .out_3(out_6), .out_4(out_5));
endmodule

module _5 (
  output out_1,
  output out_2,
  output out_3,
  output out_4
);

  wire clock_1_out, d_ff_1_q, d_ff_2_q, d_ff_3_q, d_ff_4_q;

  Clock clock_1 (.out(clock_1_out));
  D_Flip_Flop d_ff_1 (.clk(clock_1_out), .D(out_4), .Q(d_ff_1_q));  // open: Qn, preset, en, reset
  D_Flip_Flop d_ff_2 (.clk(clock_1_out), .D(out_3), .Q(d_ff_2_q));  // open: Qn, preset, en, reset
  D_Flip_Flop d_ff_3 (.clk(clock_1_out), .D(out_2), .Q(d_ff_3_q));  // open: Qn, preset, en, reset
  D_Flip_Flop d_ff_4 (.clk(clock_1_out), .D(out_1), .Q(d_ff_4_q));  // open: Qn, preset, en, reset
  _4 u_4_1 (
    .in_1(d_ff_4_q), .in_2(d_ff_3_q), .in_3(d_ff_2_q), .in_4(d_ff_1_q), .out_6(out_1), .out_7(out_2),
    .out_8(out_3), .out_9(out_4));  // open: out_5
endmodule
